# Fritzing sketch Sound Detector analog (saved by Fritzing 0.9.2b)
breadboards: 1

parts:
  PART1 = Sound Detector
  Part1 = Intel Edison Arduinobreakout

nets:
  N1: PART1.ENVELOPE, Part1.A0
  5V: PART1.VCC, Part1.5V
  GND: PART1.GND, Part1.GND

custom parts:
  Sound Detector: Electret microphone with multiple outputs. - First output is the actual audio - Second output is the amplitude envelope - Third output is a binary "sound present" indication - high while sound is present, low otherwise. Visit sparkfun.com for more documentations.
