# Fritzing sketch SI1145 Schematic, Breadboard (saved by Fritzing 0.9.2b)
breadboards: 1

parts:
  SI1145_1 = SI1145 UV Sensor [part_number="SI1145 " package="Breakout Board"]
  Part1 = Intel Edison Arduinobreakout

nets:
  VIN: SI1145_1.Vin, Part1.5V
  GND: SI1145_1.GND, Part1.GND
  N1: SI1145_1.SDA, Part1.A4/SDA
  N2: SI1145_1.SCL, Part1.A5/SCL

custom parts:
  SI1145 UV Sensor: The SI1145 is a new sensor from SiLabs with a calibrated UV sensing element that can calculate UV Index. It's a digital sensor that works over I2C so just about any microcontroller can use it. The sensor also has visible and IR sensing elements so you can measure just about any kind of light - but only the UV sensor has a calibrated output so if you need precision Lux measurement check out the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
