# Fritzing sketch Breadboard View & Schematic (saved by Fritzing 0.9.2b)
breadboards: 1

parts:
  Part1 = Intel Edison Arduinobreakout
  IC1 = TSL2561 Luminosity/Lux sensor [part_number=TSL2561 chip_label=TSL2561 package="Breakout Board"]

nets:
  N1: Part1.A4/SDA, IC1.SDA
  N2: Part1.A5/SCL, IC1.SCL
  3V3: Part1.3V3, IC1.Vin
  GND: Part1.GND, IC1.GND

custom parts:
  TSL2561 Luminosity/Lux sensor: The TSL2561 luminosity sensor is an advanced digital light sensor, ideal for use in a wide range of light situations. Compared to low cost CdS cells, this sensor is more precise, allowing for exact lux calculations and can be configured for different gain/timing ranges to detect light ranges from up to 0.1 - 40,000+ Lux on the fly. The best part of this sensor is that it contains both infrared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
