# Fritzing sketch Weather Station (saved by Fritzing 0.9.2b)
circuit board: 8.46667cm x 5.64444cm
breadboards: 1

parts:
  Part1 = Intel Edison Arduinobreakout
  MQ2 = GAS_SENSOR [package=mq-3]
  SL-HS-1 = Humidity Sensor SL-HS-220
  R1 = Temperature Sensor (Thermistor) [thermistor_type=NTC package=THT]
  IC1 = IC, DIP package, 6 pins [chip_label=ADC]
  R2 = Resistor [tolerance=±5% resistance=220 package="1206 [SMD]"]
  R3 = Resistor [tolerance=±5% resistance=220 package="1206 [SMD]"]
  Part2 = Rain Sensor YL-83 [package=molex-1x2_lock]
  Part3 = Real Time Clock Module - DS1307 RTC Breakout Board

nets:
  N1: Part1.A0, R1.pin_1, R2.Pin_0
  N2: Part1.A1, SL-HS-1.Data-signal
  N3: Part1.A2, MQ2.H1, R3.Pin_0
  N4: Part1.A4/SDA, Part3.SDA
  N5: Part1.A5/SCL, Part3.SCL
  N6: Part1.D2, IC1.pin3
  5V: Part1.5V, MQ2.B1, SL-HS-1.VCC, R1.pin_0, IC1.pin1, Part3.5V
  GND: Part1.GND, MQ2.A1, SL-HS-1.GND, IC1.pin2, R2.Pin_1, R3.Pin_1, Part3.GND
  N7: IC1.pin5, Part2.1
  N8: IC1.pin6, Part2.2

notes:
  Rain Sensor

custom parts:
  Humidity Sensor SL-HS-220: Digital relative humidity & temperature sensor SL-HS-220
